// Logisim project ShadowLockCircuit.circ as structural Verilog: 1 circuit, main circuit SHADOW
module SHADOW (
);

  wire d_ff_1_q, MREQ_out, not_1_out, not_2_out, not_3_out, or_1_out, or_2_out, RD_out, Reset_out, ROMdis_out;

  Button #(.press("passive")) MREQ (.out(MREQ_out));
  not not_1 (not_1_out, ROMdis_out);
  Button #(.press("passive")) ROMdis (.out(ROMdis_out));
  Button #(.press("passive")) Reset (.out(Reset_out));
  Button #(.press("passive")) RD (.out(RD_out));
  not not_2 (not_2_out, 1'b1);
  D_Flip_Flop d_ff_1 (.D(1'b1), .clk(not_1_out), .Q(d_ff_1_q), .preset(not_2_out), .reset(not_3_out));  // open: Qn
  not not_3 (not_3_out, Reset_out);
  or or_1 (or_1_out, MREQ_out, d_ff_1_q);
  LED ROMcs (.in(or_1_out));
  or or_2 (or_2_out, ~d_ff_1_q, RD_out);  // OR_Gate
  LED RAMoe (.in(or_2_out));
endmodule
